# Fritzing sketch AR18_2LED (saved by Fritzing 0.9.3b)
breadboards: 1

parts:
  LED1 = LED - 5mm [color="Red (633nm)" package="5 mm [THT]"]
  부품1 = Arduino Uno (Rev3)
  R2 = Resistor [tolerance=±5% resistance=220 package=THT]
  LED3 = LED - 5mm [color="Orange (612nm)" package="5 mm [THT]"]
  R1 = Resistor [tolerance=±5% resistance=220 package=THT]

nets:
  N1: LED1.cathode, R1.Pin_0
  N2: LED1.anode, 부품1.D5_PWM
  N3: 부품1.D3_PWM, LED3.anode
  N4: 부품1.GND, R2.Pin_1, R1.Pin_1
  N5: R2.Pin_0, LED3.cathode
