# Fritzing sketch AR18_4led (saved by Fritzing 0.9.3b)
breadboards: 1

parts:
  LED1 = LED - 5mm [color="Red (633nm)" package="5 mm [THT]"]
  부품1 = Arduino Uno (Rev3)
  R2 = Resistor [tolerance=±5% resistance=220 package=THT]
  LED3 = LED - 5mm [color="Orange (612nm)" package="5 mm [THT]"]
  R1 = Resistor [tolerance=±5% resistance=220 package=THT]
  LED4 = LED - 5mm [color="Blue (470nm)" package="5 mm [THT]"]
  LED5 = LED - 5mm [color="Green (565nm)" package="5 mm [THT]"]
  R3 = Resistor [tolerance=±5% resistance=220 package=THT]
  R4 = Resistor [tolerance=±5% resistance=220 package=THT]

nets:
  N1: LED1.cathode, R1.Pin_0
  N2: LED1.anode, 부품1.D5_PWM
  N3: 부품1.D9_PWM, LED5.anode
  N4: 부품1.D3_PWM, LED3.anode
  N5: 부품1.D6_PWM, LED4.anode
  N6: 부품1.GND, R2.Pin_1, R1.Pin_1, R3.Pin_1, R4.Pin_1
  N7: R2.Pin_0, LED3.cathode
  N8: LED4.cathode, R4.Pin_0
  N9: LED5.cathode, R3.Pin_0
