# Fritzing sketch 자동차 감지센서 (saved by Fritzing 0.9.10b)
breadboards: 1

parts:
  부품1 = Arduino Uno (Rev3)
  HC-SR04_Sensor_1 = HC-SR04 Ultrasonic Distance Sensor
  J1 = Piezo Speaker

nets:
  GND: 부품1.D9_PWM, 부품1.GND, HC-SR04_Sensor_1.TRIG, HC-SR04_Sensor_1.GND
  N1: 부품1.D4, HC-SR04_Sensor_1.VCC
  N2: 부품1.D5_PWM, HC-SR04_Sensor_1.ECHO
  N3: J1.pin1, J1.pin2
